# Fritzing sketch tempSensorThingsBoard_StandAlone (saved by Fritzing 0.9.3b)
circuit board: 8.46667cm x 5.64444cm
breadboards: 1

parts:
  U1 = ESP8266 WiFi Module [part_number=ESP8266]
  VCC1 = Battery
  DS1620 = IC, DIP package, 8 pins [chip_label=DS1620 part_number=DS1620]

nets (from the schematic view):
  N1: U1.VCC, U1.CH_PD, VCC1.+
  GND: U1.GPIO_0, U1.GND, VCC1.-, DS1620.pin4
  N2: U1.GPIO_2, DS1620.pin2
  N3: U1.TXD, DS1620.pin1
  3.3V: DS1620.pin8

custom parts:
  ESP8266 WiFi Module: Generic WiFi Module based on the ESP8266 with onboard PCB antenna and UART communications
