# Fritzing sketch tempSensorThingsBoard_UploadFirmware (saved by Fritzing 0.9.3b)
circuit board: 8.46667cm x 5.64444cm
breadboards: 1

parts:
  Componente1 = Arduino Uno (Rev3) - ICSP
  U1 = ESP8266 WiFi Module [part_number=ESP8266]
  VCC1 = Battery
  BATT1 = 3xAAA Switchable Battery Pack w/Bare Wire

nets:
  N1: Componente1.5V, BATT1.POS
  N2: Componente1.GND, BATT1.NEG
  N3: Componente1.D0/RX, U1.TXD
  N4: Componente1.D1/TX, U1.RXD
  N5: U1.VCC, U1.CH_PD, VCC1.+
  N6: U1.GPIO_0, U1.GND, VCC1.-

custom parts:
  ESP8266 WiFi Module: Generic WiFi Module based on the ESP8266 with onboard PCB antenna and UART communications
  3xAAA Switchable Battery Pack w/Bare Wire: 3xAAA Switchable Battery Pack w/Bare Wire Connectors
